# Fritzing sketch fencing001 (saved by Fritzing 0.8.3b)
breadboards: 2

parts:
  Part1 = Arduino Uno (Rev3)
  Part2 = SRF05 Ultrasonic Rangefinder
  Part3 = SRF05 Ultrasonic Rangefinder
  LED1 = LED - 5mm [color="Green (555nm)" package="5 mm [THT]"]
  LED2 = LED - 5mm [color="Red (633nm)" package="5 mm [THT]"]
  R1 = Resistor [tolerance=±5% resistance=470 package=THT]
  R2 = Resistor [tolerance=±5% resistance=470 package=THT]

nets:
  GND: Part1.GND, Part3.GND, R1.Pin_0, R2.Pin_0
  N1: Part1.D8, Part3.Echo
  N2: Part1.D9_PWM, Part3.Trig
  N3: Part1.D10_PWM/SS, LED1.anode
  N4: Part1.D11_PWM/MOSI, LED2.anode
  N5: Part1.D12/MISO, Part2.Echo
  N6: Part1.D13/SCK, Part2.Trig
  5V: Part1.5V, Part3.VCC
  N7: LED1.cathode, R2.Pin_1
  N8: LED2.cathode, R1.Pin_1
